# Fritzing sketch Nightlight (saved by Fritzing 0.9.3b)

parts:
  U1 = Explorer HAT Pro [part_number="Explorer HAT Pro" package=THT]
  R1 = Photocell (LDR) [package=THT]  # not connected
  R2 = Resistor [tolerance=±5% resistance=22k package=THT]  # not connected
  Raspberry_Pi_1 = Raspberry Pi 3 [part_number=RPI-3-V1.2]  # not connected

nets:
  N1: U1.F11, U1.G11, U1.J11, U1.Analog_1
  N2: U1.F15, U1.J15, U1.POW3V3
  N3: U1.G6, U1.J6, U1.Ground

custom parts:
  Explorer HAT Pro: Explorer HAT Pro with 4 Output and 4 Input connections, 4 Analog Inputs and 2 bi-directional motor channels, plus power and ground.
