# Fritzing sketch candle (saved by Fritzing 0.9.3b)

parts:
  Raspberry_Pi_1 = Raspberry Pi 3 [part_number=RPI-3-V1.2]  # not connected
  U1 = Explorer HAT Pro [part_number="Explorer HAT Pro" package=THT]
  Part2 = Breakout Board for Electret Microphone

nets:
  5V: U1.5v, U1.G2, U1.J2, Part2.VCC
  N1: U1.G3, U1.H3, U1.Ground, Part2.GND
  N2: U1.G4, U1.I4, U1.Analog_1, Part2.AUD

custom parts:
  Explorer HAT Pro: Explorer HAT Pro with 4 Output and 4 Input connections, 4 Analog Inputs and 2 bi-directional motor channels, plus power and ground.
